# Fritzing sketch layout (saved by Fritzing 0.9.3b)
breadboards: 1

parts:
  Part1 = Arduino Uno (Rev3) - ICSP
  C1 = Capacitor Polarized [package=panasonic_d]
  R1 = Resistor [tolerance=±5% resistance=1k package=THT]
  LED1 = smd LED [color="Yellow (595nm)" package="1206 [SMD]"]
  C2 = Capacitor Polarized [package=panasonic_d]
  Part2 = LED Matrix - Serial Interface - Red/Green/Blue
  M1 = fc-51 [package=THT]
  J1 = Piezo Speaker
  C3 = Capacitor Polarized [package=panasonic_d]
  U1 = Molex Picoblade Series Header [part_number=0532610219 package=Picoblade-53261-0219]
  C4 = Capacitor Polarized [package=panasonic_d]
  M2 = Dagu DGServo 9g (Top view) [part_number=RS001B]
  M3 = Dagu DGServo 9g (Top view) [part_number=RS001B]
  C5 = Capacitor Polarized [package=panasonic_d]

nets:
  GND: Part1.GND, C1.-, R1.Pin_0, C2.-, Part2.GND, M1.pin2, J1.pin1, C3.-, U1.2, C4.-, M2.gnd, M3.gnd, C5.-
  N1: Part1.D9_PWM, M3.pulse
  N2: Part1.D10_PWM/SS, M2.pulse
  N3: Part1.D2, M1.pin1
  N4: Part1.D3_PWM, J1.pin2
  N5: Part1.D4, Part2.MOSI
  N6: Part1.D5_PWM, Part2.CS
  N7: Part1.D6_PWM, Part2.SCK
  5V: Part1.5V, C1.+, C2.+, Part2.VCC, M1.pin3, C3.+
  N8: R1.Pin_1, LED1.cathode
  VCC: LED1.anode, U1.1, C4.+, M2.vcc, M3.vcc, C5.+
